# Fritzing sketch waterpump-ctrl-docs-v1 (saved by Fritzing 0.9.4)
circuit board: 7.87582cm x 5.55789cm
breadboards: 1

parts:
  U3 = TRIAC [part_number=BT139 package=to-220]
  R3 = Resistor [tolerance=±5% resistance=330 power=1W part_number=360Ohms package=THT]
  R4 = Resistor [tolerance=±5% resistance=470 power=1W package=THT]
  R5 = Resistor [tolerance=±5% resistance=33 power=1W part_number="39 Ohms" package=THT]
  U2 = MOC3031-M [part_number=MOC3021 package=dil06]
  C2 = Film/Foil Capacitor [capacitance=100nF voltage=35V part_number=0.01uF/400V package="7.5mm [THT, pp]"]
  C1 = Film/Foil Capacitor [capacitance=100nF voltage=35V part_number=0.05uF/400V package="7.5mm [THT, pp]"]
  J2 = rounded female pin header, 4 pins [form="♀ (female rounded)"]
  VCC1 = 4 x AAA Battery Mount
  R1 = Resistor [tolerance=±5% resistance=220 package=THT]
  S2 = Square Pushbutton
  J1 = rounded female pin header, 2 pins [form="♀ (female rounded)"]
  U1 = NodeMCU V3.0

nets:
  N1: U3.MT1, C2.+, C1.+, J1.pin1
  N2: U3.G, U2.4
  N3: U3.MT2, R4.Pin_1, R5.Pin_0, J1.pin2
  N4: R3.Pin_0, U2.6
  N5: R3.Pin_1, R4.Pin_0, C1.-
  N6: R5.Pin_1, C2.-
  N7: U2.1, U1.D6
  GND: U2.2, J2.pin4, VCC1.-, S2.leg1, U1.GND#6, U1.GND#13, U1.GND#16, U1.GND#33
  N8: J2.pin1, U1.D2
  N9: J2.pin2, U1.D1
  N10: J2.pin3, R1.Pin_0, U1.3V3
  N11: VCC1.+, U1.Vin
  N12: R1.Pin_1, S2.leg0, U1.D7

custom parts:
  TRIAC: Generic TRIAC, TO-220 package
  NodeMCU V3.0: ESP8266 based NodeMCU
